# Fritzing sketch pool_automation (saved by Fritzing 0.9.2b)

parts:
  Raspberry_Pi1 = Raspberry Pi 2  # not connected
  R1 = Resistor [tolerance=±1% resistance=330 package=THT]
  S1 = Pushbutton [package=THT]
  S2 = Pushbutton [package=THT]
  S3 = Pushbutton [package=THT]
  UniPi3 = UniPi v1.1

nets:
  N1: R1.Pin_0, UniPi3.12V
  N2: R1.Pin_1, S1.leg1
  N3: S1.leg0, UniPi3.I01
  N4: S2.leg0, UniPi3.Rel1_NO
  N5: S3.leg0, UniPi3.Rel2_NO

custom parts:
  UniPi v1.1: UniPi is an add-on expansion board for the Raspberry Pi. It features many components such as digital galvanicaly isolated inputs with LED signalization, 0-10V analog inputs, 0-10V analog outputs, changeover relays, single channel 1wire master controller and a real-time clock module.
