# Fritzing sketch blink (saved by Fritzing 0.8.7b)
breadboards: 1

parts:
  R3 = Resistor [tolerance=±5% resistance=330 package=THT]
  LED1 = LED - 3mm [color="Red (633nm)" package="3 mm [THT]"]
  LED3 = LED - 3mm [color="Yellow (595nm)" package="3 mm [THT]"]
  R4 = Resistor [tolerance=±5% resistance=330 package=THT]
  LED4 = LED - 3mm [color="Green (555nm)" package="3 mm [THT]"]
  R5 = Resistor [tolerance=±5% resistance=330 package=THT]
  Raspberry_Pi_B_rev1 = Raspberry Pi B rev2

nets:
  N1: R3.Pin_0, LED4.cathode
  N2: R3.Pin_1, LED3.anode, R4.Pin_1, LED4.anode, R5.Pin_1, Raspberry_Pi_B_rev1.GND, Raspberry_Pi_B_rev1.GPIO_23, Raspberry_Pi_B_rev1.GPIO_14, Raspberry_Pi_B_rev1.GPIO_24
  N3: LED1.cathode, R5.Pin_0
  N4: LED1.anode, Raspberry_Pi_B_rev1.GPIO_25, Raspberry_Pi_B_rev1.GPIO_8
  N5: LED3.cathode, R4.Pin_0
