# Fritzing sketch thermostat (saved by Fritzing 0.9.2b)
breadboards: 1

parts:
  U1 = 2-Channel 5v Relay Shield [package=relay-2ch5v10a]
  Raspberry_Pi1 = Raspberry Pi 2
  R1 = Resistor [tolerance=±5% resistance=4.7k package=THT]
  T1 = DS18B20 Sensor [part_number=DS18B20 package="TO92 [THT]"]

nets:
  VCC: U1.VCC, Raspberry_Pi1.5V
  GND: U1.GND, Raspberry_Pi1.GND, T1.GND
  N1: U1.IN1, Raspberry_Pi1.GPIO17
  N2: Raspberry_Pi1.3v3, R1.Pin_1, T1.+Vdd
  N3: Raspberry_Pi1.GPIO4, R1.Pin_0, T1.DQ

notes:
  R=4k7

custom parts:
  2-Channel 5v Relay Shield: 2 Channel 5v Relay Shield w. 2x SPD-06VDC-SD-C
  DS18B20 Sensor: A DS18B20 temperature sensor
