# Fritzing sketch LEDsnake (saved by Fritzing 0.9.2b)
breadboards: 1

parts:
  Raspberry_Pi1 = Raspberry Pi 2  # not connected
  S1 = Pushbutton [package=THT]
  R1 = Resistor [tolerance=±5% resistance=330 package=THT]
  S2 = Pushbutton [package=THT]
  S3 = Pushbutton [package=THT]
  S4 = Pushbutton [package=THT]
  R2 = Resistor [tolerance=±5% resistance=330 package=THT]
  S5 = Pushbutton [package=THT]
  S6 = Pushbutton [package=THT]
  UniPi1 = UniPi v1.1

nets:
  N1: S1.leg0, S2.leg0, S3.leg0, S4.leg0, UniPi1.I01, UniPi1.I02, UniPi1.I03, UniPi1.I04
  N2: S1.leg1, R1.Pin_1, S2.leg1, S3.leg1, S4.leg1
  N3: R1.Pin_0, R2.Pin_0, UniPi1.12V
  N4: R2.Pin_1, S5.leg0, S6.leg0
  N5: S5.leg1, S6.leg1, UniPi1.I05, UniPi1.I06

custom parts:
  UniPi v1.1: UniPi is an add-on expansion board for the Raspberry Pi. It features many components such as digital galvanicaly isolated inputs with LED signalization, 0-10V analog inputs, 0-10V analog outputs, changeover relays, single channel 1wire master controller and a real-time clock module.
